# Fritzing sketch Ladder Filter Curren Source MiniMoog (saved by Fritzing 0.9.3b)
breadboards: 1

parts:
  Q1 = NPN-Transistor [package="TO92 [THT]"]
  Q2 = PNP-Transistor [package="TO92 [THT]"]
  R1 = Resistor [tolerance=±5% resistance=47k package=THT]
  R2 = Resistor [tolerance=±5% resistance=4.7k package=THT]
  R3 = Resistor [tolerance=±5% resistance=330 package=THT]
  R4 = Resistor [tolerance=±5% resistance=68k package=THT]
  R5 = Resistor [tolerance=±5% resistance=10k package=THT]
  C1 = Electrolytic Capacitor [capacitance=1µF package="100 mil [THT, electrolytic]"]
  R6 = TRIMPOT [package=trimpot_pth_s3_lock]

nets:
  N1: Q1.E, R2.Pin_1, R3.Pin_1, C1.-, R6.CCW
  N2: Q1.B, R5.Pin_0
  N3: Q1.C, Q2.E, R4.Pin_1
  N4: Q2.B, R3.Pin_0
  N5: Q2.C, R1.Pin_0, R2.Pin_0
  N6: R4.Pin_0, R6.WIPER
  N7: R5.Pin_1, C1.+, R6.CW

notes:
  IN
  OUT
  GND
  VCC
  2SC1814 / 2SA1015
  E/C/B
