# Fritzing sketch Ladder Filter Curren Source_og3  (saved by Fritzing 0.9.3b)
breadboards: 1

parts:
  R1 = Resistor [tolerance=±5% resistance=22k package=THT]
  R2 = Resistor [tolerance=±5% resistance=1k package=THT]
  Q1 = NPN-Transistor [package="TO92 [THT]"]
  Q2 = NPN-Transistor [package="TO92 [THT]"]
  R3 = Resistor [tolerance=±5% resistance=4.7k package=THT]
  R4 = Resistor [tolerance=±5% resistance=330 package=THT]
  R5 = Resistor [tolerance=±5% resistance=6.8k package=THT]
  IC1 = Dual Op-Amp [package=dip08]
  C2 = Ceramic Capacitor [capacitance=100nF package="100 mil [THT, multilayer]"]
  C3 = Ceramic Capacitor [capacitance=100nF package="100 mil [THT, multilayer]"]
  C4 = Ceramic Capacitor [capacitance=100nF package="100 mil [THT, multilayer]"]
  C5 = Electrolytic Capacitor [capacitance=1µF package="100 mil [THT, electrolytic]"]
  C6 = Electrolytic Capacitor [capacitance=1µF package="100 mil [THT, electrolytic]"]

nets:
  N1: R1.Pin_0, R2.Pin_0, Q1.C
  N2: R2.Pin_1, Q2.C, IC1.A_+IN, IC1.B_+IN, C2.0, C4.0, C5.-, C6.+
  N3: Q1.E, Q2.E, R4.Pin_1
  N4: Q1.B, R3.Pin_1
  N5: Q2.B, R5.Pin_1, IC1.B_-IN, C3.1
  N6: R3.Pin_0, R5.Pin_0, IC1.A_V+, C2.1, C5.+
  N7: R4.Pin_0, IC1.B_OUT, C3.0
  N8: IC1.A_OUT, IC1.A_-IN
  N9: IC1.A_V-, C4.1, C6.-

notes:
  GND
  VCC
  VEE
  GND
  OUT
  IN
  2SC1814
  E/C/B
